// Logisim project Representação C2 - SomadorSubtrador.circ as structural Verilog: 1 circuit, main circuit main
module main (
  input  A0,
  input  B0,
  input  C0,
  input  D0,
  output A1,
  output B1,
  output C1,
  output D1
);

  wire complementodois_1_a1, complementodois_1_b1, complementodois_1_c1, complementodois_1_d1, demux_21_1_s0,
       demux_21_1_s1, demux_21_2_s0, demux_21_2_s1, demux_21_3_s0, demux_21_3_s1, demux_21_4_s0,
       demux_21_4_s1;

  Demux_21 demux_21_1 (.E(A0), .A(A0), .S0(demux_21_1_s0), .S1(demux_21_1_s1));
  Demux_21 demux_21_2 (.E(B0), .A(A0), .S0(demux_21_2_s0), .S1(demux_21_2_s1));
  Demux_21 demux_21_3 (.E(C0), .A(A0), .S0(demux_21_3_s0), .S1(demux_21_3_s1));
  Demux_21 demux_21_4 (.E(D0), .A(A0), .S0(demux_21_4_s0), .S1(demux_21_4_s1));
  or or_1 (A1, demux_21_1_s0, complementodois_1_a1);
  or or_2 (B1, demux_21_2_s0, complementodois_1_b1);
  ComplementoDois complementodois_1 (
    .A0(demux_21_1_s1), .B0(demux_21_2_s1), .C0(demux_21_3_s1), .D0(demux_21_4_s1),
    .A1(complementodois_1_a1), .B1(complementodois_1_b1), .C1(complementodois_1_c1), .D1(complementodois_1_d1));
  or or_3 (D1, demux_21_4_s0, complementodois_1_d1);
  or or_4 (C1, demux_21_3_s0, complementodois_1_c1);
endmodule
