// Logisim project Somador - 4 Bits.circ as structural Verilog: 1 circuit, main circuit main
module main (
  input  A3,
  input  A2,
  input  A1,
  input  A0,
  input  B3,
  input  B2,
  input  B1,
  input  B0
);

  wire hexadecimal_1_p5, hexadecimal_1_p6, hexadecimal_1_p7, hexadecimal_1_p8, hexadecimal_1_p9,
       hexadecimal_1_p10, hexadecimal_1_p11, main_1_s0, main_1_s1, main_1_s2, main_1_s3;

  Biblioteca___Somador01_main main_1 (
    .B3(B3), .A3(A3), .B2(B2), .A2(A2), .B1(B1), .A1(A1), .B0(B0), .A0(A0), .S3(main_1_s3), .S2(main_1_s2),
    .S1(main_1_s1), .S0(main_1_s0));
  // Hexadecimal hexadecimal_1: pin names not known; wires that end beside it: main_1_s3, main_1_s2, main_1_s1, main_1_s0, hexadecimal_1_p5, hexadecimal_1_p6, hexadecimal_1_p7, hexadecimal_1_p8, hexadecimal_1_p9, hexadecimal_1_p10, hexadecimal_1_p11
  _7_Segment_Display u_7_segment_display_1 (
    .g(hexadecimal_1_p11), .f(hexadecimal_1_p10), .a(hexadecimal_1_p5), .b(hexadecimal_1_p6),
    .e(hexadecimal_1_p9), .d(hexadecimal_1_p8), .c(hexadecimal_1_p7));  // open: dp
endmodule
