// Logisim project Codificador.circ as structural Verilog: 1 circuit, main circuit Codificador
module Codificador (
  input  a,
  input  b,
  input  c,
  input  d,
  input  e,
  input  f,
  input  g,
  input  h,
  input  i,
  input  j,
  output a_2,
  output b_2,
  output c_2,
  output d_2
);

  wire and_1_out, and_2_out, and_3_out, and_4_out, and_5_out, and_6_out, and_7_out, and_8_out, and_9_out,
       and_10_out, and_11_out, and_12_out, and_13_out, and_14_out, and_15_out, not_1_out, not_2_out,
       not_3_out, not_4_out, not_5_out, not_6_out, not_7_out, not_8_out, not_9_out, not_10_out, not_11_out,
       not_12_out, not_13_out, not_14_out, not_15_out, not_16_out, not_17_out, not_18_out, not_19_out,
       not_20_out, not_21_out, not_22_out, not_23_out, not_24_out, not_25_out, not_26_out, not_27_out,
       not_28_out, not_29_out, not_30_out, not_31_out, not_32_out, not_33_out, not_34_out, not_35_out,
       not_36_out, not_37_out, not_38_out, not_39_out, not_40_out, not_41_out, not_42_out, not_43_out,
       not_44_out, not_45_out, not_46_out, not_47_out, not_48_out, not_49_out, not_50_out, not_51_out,
       not_52_out, not_53_out, not_54_out, not_55_out, not_56_out, not_57_out, not_58_out, not_59_out,
       not_60_out, not_61_out, not_62_out, not_63_out, not_64_out, not_65_out, not_66_out, not_67_out,
       not_68_out, not_69_out, not_70_out, not_71_out, not_72_out, not_73_out, not_74_out, not_75_out,
       not_76_out, not_77_out, not_78_out, not_79_out, not_80_out, not_81_out, not_82_out, not_83_out,
       not_84_out, not_85_out, not_86_out, not_87_out, not_88_out, not_89_out, not_90_out, not_91_out,
       not_92_out, not_93_out, not_94_out, not_95_out, not_96_out, not_97_out, not_98_out, not_99_out,
       not_100_out, not_101_out, not_102_out, not_103_out, not_104_out, not_105_out, not_106_out,
       not_107_out, not_108_out, not_109_out, not_110_out, not_111_out, not_112_out, not_113_out,
       not_114_out, not_115_out, not_116_out, not_117_out, not_118_out, not_119_out, not_120_out,
       not_121_out, not_122_out, not_123_out, not_124_out, not_125_out, not_126_out, not_127_out,
       not_128_out, not_129_out, not_130_out, not_131_out, not_132_out, not_133_out, not_134_out, not_135_out;

  not not_1 (not_1_out, a);
  not not_2 (not_2_out, b);
  not not_3 (not_3_out, c);
  not not_4 (not_4_out, d);
  not not_5 (not_5_out, e);
  not not_6 (not_6_out, f);
  not not_7 (not_7_out, g);
  not not_8 (not_8_out, h);
  not not_9 (not_9_out, j);
  not not_10 (not_10_out, a);
  not not_11 (not_11_out, b);
  not not_12 (not_12_out, c);
  not not_13 (not_13_out, d);
  not not_14 (not_14_out, e);
  not not_15 (not_15_out, f);
  not not_16 (not_16_out, g);
  not not_17 (not_17_out, i);
  not not_18 (not_18_out, j);
  not not_19 (not_19_out, a);
  not not_20 (not_20_out, b);
  not not_21 (not_21_out, c);
  not not_22 (not_22_out, d);
  not not_23 (not_23_out, e);
  not not_24 (not_24_out, f);
  not not_25 (not_25_out, h);
  not not_26 (not_26_out, i);
  not not_27 (not_27_out, j);
  not not_28 (not_28_out, a);
  not not_29 (not_29_out, b);
  not not_30 (not_30_out, c);
  not not_31 (not_31_out, d);
  not not_32 (not_32_out, e);
  not not_33 (not_33_out, g);
  not not_34 (not_34_out, h);
  not not_35 (not_35_out, i);
  not not_36 (not_36_out, j);
  not not_37 (not_37_out, a);
  not not_38 (not_38_out, b);
  not not_39 (not_39_out, c);
  not not_40 (not_40_out, d);
  not not_41 (not_41_out, f);
  not not_42 (not_42_out, g);
  not not_43 (not_43_out, h);
  not not_44 (not_44_out, i);
  not not_45 (not_45_out, j);
  not not_46 (not_46_out, a);
  not not_47 (not_47_out, b);
  not not_48 (not_48_out, c);
  not not_49 (not_49_out, e);
  not not_50 (not_50_out, f);
  not not_51 (not_51_out, g);
  not not_52 (not_52_out, h);
  not not_53 (not_53_out, i);
  not not_54 (not_54_out, j);
  not not_55 (not_55_out, a);
  not not_56 (not_56_out, b);
  not not_57 (not_57_out, c);
  not not_58 (not_58_out, d);
  not not_59 (not_59_out, e);
  not not_60 (not_60_out, f);
  not not_61 (not_61_out, h);
  not not_62 (not_62_out, i);
  not not_63 (not_63_out, j);
  not not_64 (not_64_out, a);
  not not_65 (not_65_out, b);
  not not_66 (not_66_out, c);
  not not_67 (not_67_out, d);
  not not_68 (not_68_out, e);
  not not_69 (not_69_out, g);
  not not_70 (not_70_out, h);
  not not_71 (not_71_out, i);
  not not_72 (not_72_out, j);
  not not_73 (not_73_out, a);
  not not_74 (not_74_out, b);
  not not_75 (not_75_out, d);
  not not_76 (not_76_out, e);
  not not_77 (not_77_out, f);
  not not_78 (not_78_out, g);
  not not_79 (not_79_out, h);
  not not_80 (not_80_out, i);
  not not_81 (not_81_out, j);
  not not_82 (not_82_out, a);
  not not_83 (not_83_out, c);
  not not_84 (not_84_out, d);
  not not_85 (not_85_out, e);
  not not_86 (not_86_out, f);
  not not_87 (not_87_out, g);
  not not_88 (not_88_out, h);
  not not_89 (not_89_out, i);
  not not_90 (not_90_out, j);
  not not_91 (not_91_out, a);
  not not_92 (not_92_out, b);
  not not_93 (not_93_out, c);
  not not_94 (not_94_out, d);
  not not_95 (not_95_out, e);
  not not_96 (not_96_out, f);
  not not_97 (not_97_out, g);
  not not_98 (not_98_out, h);
  not not_99 (not_99_out, j);
  not not_100 (not_100_out, a);
  not not_101 (not_101_out, b);
  not not_102 (not_102_out, c);
  not not_103 (not_103_out, d);
  not not_104 (not_104_out, e);
  not not_105 (not_105_out, f);
  not not_106 (not_106_out, h);
  not not_107 (not_107_out, i);
  not not_108 (not_108_out, j);
  not not_109 (not_109_out, a);
  not not_110 (not_110_out, b);
  not not_111 (not_111_out, c);
  not not_112 (not_112_out, d);
  not not_113 (not_113_out, f);
  not not_114 (not_114_out, g);
  not not_115 (not_115_out, h);
  not not_116 (not_116_out, i);
  not not_117 (not_117_out, j);
  not not_118 (not_118_out, a);
  not not_119 (not_119_out, b);
  not not_120 (not_120_out, d);
  not not_121 (not_121_out, e);
  not not_122 (not_122_out, f);
  not not_123 (not_123_out, g);
  not not_124 (not_124_out, h);
  not not_125 (not_125_out, i);
  not not_126 (not_126_out, j);
  not not_127 (not_127_out, b);
  not not_128 (not_128_out, c);
  not not_129 (not_129_out, d);
  not not_130 (not_130_out, e);
  not not_131 (not_131_out, f);
  not not_132 (not_132_out, g);
  not not_133 (not_133_out, h);
  not not_134 (not_134_out, i);
  not not_135 (not_135_out, j);
  and and_1 (and_1_out, not_1_out, not_2_out, not_3_out, not_4_out, not_5_out, not_6_out, not_7_out, not_8_out, i, not_9_out);
  and and_2 (and_2_out, not_10_out, not_11_out, not_12_out, not_13_out, not_14_out, not_15_out, not_16_out, h, not_17_out, not_18_out);
  and and_3 (and_3_out, not_19_out, not_20_out, not_21_out, not_22_out, not_23_out, not_24_out, g, not_25_out, not_26_out, not_27_out);
  and and_4 (and_4_out, not_28_out, not_29_out, not_30_out, not_31_out, not_32_out, f, not_33_out, not_34_out, not_35_out, not_36_out);
  and and_5 (and_5_out, not_37_out, not_38_out, not_39_out, not_40_out, e, not_41_out, not_42_out, not_43_out, not_44_out, not_45_out);
  and and_6 (and_6_out, not_46_out, not_47_out, not_48_out, d, not_49_out, not_50_out, not_51_out, not_52_out, not_53_out, not_54_out);
  and and_7 (and_7_out, not_55_out, not_56_out, not_57_out, not_58_out, not_59_out, not_60_out, g, not_61_out, not_62_out, not_63_out);
  and and_8 (and_8_out, not_64_out, not_65_out, not_66_out, not_67_out, not_68_out, f, not_69_out, not_70_out, not_71_out, not_72_out);
  and and_9 (and_9_out, not_73_out, not_74_out, c, not_75_out, not_76_out, not_77_out, not_78_out, not_79_out, not_80_out, not_81_out);
  and and_10 (and_10_out, not_82_out, b, not_83_out, not_84_out, not_85_out, not_86_out, not_87_out, not_88_out, not_89_out, not_90_out);
  and and_11 (and_11_out, not_91_out, not_92_out, not_93_out, not_94_out, not_95_out, not_96_out, not_97_out, not_98_out, i, not_99_out);
  and and_12 (and_12_out, not_100_out, not_101_out, not_102_out, not_103_out, not_104_out, not_105_out, g, not_106_out, not_107_out, not_108_out);
  and and_13 (and_13_out, not_109_out, not_110_out, not_111_out, not_112_out, e, not_113_out, not_114_out, not_115_out, not_116_out, not_117_out);
  and and_14 (and_14_out, not_118_out, not_119_out, c, not_120_out, not_121_out, not_122_out, not_123_out, not_124_out, not_125_out, not_126_out);
  and and_15 (and_15_out, a, not_127_out, not_128_out, not_129_out, not_130_out, not_131_out, not_132_out, not_133_out, not_134_out, not_135_out);
  or or_1 (a_2, and_1_out, and_2_out);
  or or_2 (b_2, and_3_out, and_4_out, and_5_out, and_6_out);
  or or_3 (c_2, and_7_out, and_8_out, and_9_out, and_10_out);
  or or_4 (d_2, and_11_out, and_12_out, and_13_out, and_14_out, and_15_out);
endmodule
