// Logisim project Contador - 0 até 99.circ as structural Verilog: 1 circuit, main circuit main
module main (
);

  wire and_1_out, clock_1_out, decinall_1_a_2, decinall_1_b_2, decinall_1_c_2, decinall_1_d_2, decinall_1_e,
       decinall_1_f, decinall_1_g, decinall_2_a_2, decinall_2_b_2, decinall_2_c_2, decinall_2_d_2,
       decinall_2_e, decinall_2_f, decinall_2_g, main_1_q0, main_1_q1, main_1_q2, main_1_q3, main_2_q0,
       main_2_q1, main_2_q2, main_2_q3, not_1_out;

  and and_1 (and_1_out, decinall_2_f, decinall_2_e, decinall_2_a_2, not_1_out, decinall_2_b_2, decinall_2_c_2, decinall_2_d_2);
  Clock clock_1 (.out(clock_1_out));
  \Pré_contador___0_até_99__main  main_1 (
    .Clock(clock_1_out), .Q3(main_1_q3), .Q2(main_1_q2), .Q1(main_1_q1), .Q0(main_1_q0));
  \Pré_contador___0_até_99__main  main_2 (
    .Clock(and_1_out), .Q3(main_2_q3), .Q2(main_2_q2), .Q1(main_2_q1), .Q0(main_2_q0));
  Decinall decinall_1 (
    .A(main_2_q3), .B(main_2_q2), .a_2(decinall_1_a_2), .C(main_2_q1), .D(main_2_q0), .b_2(decinall_1_b_2),
    .c_2(decinall_1_c_2), .d_2(decinall_1_d_2), .e(decinall_1_e), .f(decinall_1_f), .g(decinall_1_g));
  Decinall decinall_2 (
    .A(main_1_q3), .B(main_1_q2), .a_2(decinall_2_a_2), .C(main_1_q1), .D(main_1_q0), .b_2(decinall_2_b_2),
    .c_2(decinall_2_c_2), .d_2(decinall_2_d_2), .e(decinall_2_e), .f(decinall_2_f), .g(decinall_2_g));
  _7_Segment_Display u_7_segment_display_1 (
    .g(decinall_1_g), .f(decinall_1_f), .a(decinall_1_a_2), .b(decinall_1_b_2), .e(decinall_1_e),
    .d(decinall_1_d_2), .c(decinall_1_c_2));  // open: dp
  not not_1 (not_1_out, decinall_2_g);
  _7_Segment_Display u_7_segment_display_2 (
    .g(decinall_2_g), .f(decinall_2_f), .a(decinall_2_a_2), .b(decinall_2_b_2), .e(decinall_2_e),
    .d(decinall_2_d_2), .c(decinall_2_c_2));  // open: dp
endmodule
