// Logisim project Pré-contador - 0 até 99 .circ as structural Verilog: 1 circuit, main circuit main
module main (
  input  Clock,
  output Q3,
  output Q2,
  output Q1,
  output Q0
);

  wire and_1_out, and_2_out, and_3_out, decinall_1_a_2, decinall_1_b_2, decinall_1_c_2, decinall_1_d_2,
       decinall_1_e, decinall_1_f, decinall_1_g, Q3_qn;

  and and_1 (and_1_out, Q2, and_2_out);
  J_K_Flip_Flop u_Q3 (.J(and_1_out), .clk(Clock), .K(Q0), .Q(Q3), .Qn(Q3_qn));  // open: preset, en, reset
  J_K_Flip_Flop u_Q2 (.J(and_2_out), .clk(Clock), .K(and_2_out), .Q(Q2));  // open: Qn, preset, en, reset
  and and_2 (and_2_out, Q1, Q0);
  and and_3 (and_3_out, Q3_qn, Q0);
  J_K_Flip_Flop u_Q1 (.J(and_3_out), .clk(Clock), .K(Q0), .Q(Q1));  // open: Qn, preset, en, reset
  J_K_Flip_Flop u_Q0 (.J(1'b1), .clk(Clock), .K(1'b1), .Q(Q0));  // open: Qn, preset, en, reset
  Decinall decinall_1 (
    .A(Q3), .B(Q2), .a_2(decinall_1_a_2), .C(Q1), .D(Q0), .b_2(decinall_1_b_2), .c_2(decinall_1_c_2),
    .d_2(decinall_1_d_2), .e(decinall_1_e), .f(decinall_1_f), .g(decinall_1_g));
  _7_Segment_Display u_7_segment_display_1 (
    .g(decinall_1_g), .f(decinall_1_f), .a(decinall_1_a_2), .b(decinall_1_b_2), .e(decinall_1_e),
    .d(decinall_1_d_2), .c(decinall_1_c_2));  // open: dp
endmodule
