// Logisim project Pré-contador - 7 até 0.circ as structural Verilog: 1 circuit, main circuit main
module main (
);

  wire and_1_out, clock_1_out, decodificador09_1_p5, decodificador09_1_p6, decodificador09_1_p7,
       decodificador09_1_p8, decodificador09_1_p9, decodificador09_1_p10, decodificador09_1_p11, Q0_q, Q0_qn,
       Q1_q, Q1_qn, Q2_q;

  and and_1 (and_1_out, Q0_qn, Q1_qn);
  Clock clock_1 (.out(clock_1_out));
  J_K_Flip_Flop Q2 (.J(and_1_out), .clk(clock_1_out), .K(and_1_out), .Q(Q2_q));  // open: Qn, preset, en, reset
  J_K_Flip_Flop Q1 (.J(Q0_qn), .clk(clock_1_out), .K(Q0_qn), .Q(Q1_q), .Qn(Q1_qn));  // open: preset, en, reset
  J_K_Flip_Flop Q0 (.J(1'b1), .clk(clock_1_out), .K(1'b1), .Q(Q0_q), .Qn(Q0_qn));  // open: preset, en, reset
  // Decodificador09 decodificador09_1: pin names not known; wires that end beside it: 1'b0, Q2_q, Q1_q, Q0_q, decodificador09_1_p5, decodificador09_1_p6, decodificador09_1_p7, decodificador09_1_p8, decodificador09_1_p9, decodificador09_1_p10, decodificador09_1_p11
  _7_Segment_Display u_7_segment_display_1 (
    .g(decodificador09_1_p11), .f(decodificador09_1_p10), .a(decodificador09_1_p5), .b(decodificador09_1_p6),
    .e(decodificador09_1_p9), .d(decodificador09_1_p8), .c(decodificador09_1_p7));  // open: dp
endmodule
